# Fritzing sketch ContadorDePessoas (saved by Fritzing 0.9.4)
circuit board: 9.03748cm x 6.23156cm

parts:
  U2 = ESP8266 NodeMCU LoLin module
  LM2 = Capteur IR CAP227 - 3 pins [package=THT]
  DHT1 = Humidity and Temperature Sensor DHT11
  LM1 = Capteur IR CAP227 - 3 pins [package=THT]

nets:
  N1: U2.D3, DHT1.Data-signal
  3V3: U2.3V3, LM2.pin3, DHT1.Vcc, LM1.pin3
  N2: U2.GND, LM2.pin1, DHT1.GND_1, DHT1.GND_2, LM1.pin1
  N3: U2.D6, LM1.pin2
  N4: U2.D7, LM2.pin2

custom parts:
  ESP8266 NodeMCU LoLin module: ESP8266 based NodeMCU
  Capteur IR CAP227 - 3 pins: Capteur IR pour suiveur de ligne CAP227 A base de LM 393 Créateur : Gaetan Brissot Fournisseur : centralmedia.fr
  Humidity and Temperature Sensor DHT11: Digital relative humidity & temperature sensor DHT11
